// Logisim project Alu-final.circ as structural Verilog: 4 circuits, main circuit 1 bit Alu
module _1_bit_Alu (
  input  Cin,
  input  A,
  input  Less,
  input  B,
  input  B_invert,
  input  [2:0] op_code,
  output Set,
  output Result,
  output out_9
);

  wire and_1_out, multiplexer_1_out, not_1_out, not_2_out, or_1_out;

  not not_1 (not_1_out, B);
  Multiplexer #(.enable("false")) multiplexer_1 (.in0(B), .in1(not_1_out), .out(multiplexer_1_out), .sel(B_invert));
  Adder #(.width(1)) adder_1 (.a(A), .b(multiplexer_1_out), .out(Set), .cin(Cin), .cout(out_9));
  and and_1 (and_1_out, B, A);
  or or_1 (or_1_out, B, A);
  not not_2 (not_2_out, or_1_out);
  Multiplexer #(.select(3), .enable("false")) multiplexer_2 (
    .in0(Set), .in1(and_1_out), .in2(or_1_out), .in3(not_2_out), .in4(Less), .out(Result), .sel(op_code));  // open: in5, in6, in7

  // Notes on the sheet:
  //   ADD / SUB/ ADDI
  //   AND
  //   OR
  //   NOR
  //   Slt
  //   Carry Out
endmodule

module _16_bit_Alu (
  input  Bin,
  input  Cin,
  input  [2:0] Alu_Op,
  input  [15:0] A_input,
  input  [15:0] in_5,
  output [15:0] out_6,
  output Zero_detector,
  output out_8,
  output Set_less_than
);

  wire n1_bit_alu_1_out_9, n1_bit_alu_2_out_9, n1_bit_alu_3_out_9, n1_bit_alu_4_out_9, n1_bit_alu_5_out_9,
       n1_bit_alu_6_out_9, n1_bit_alu_7_out_9, n1_bit_alu_8_out_9, n1_bit_alu_9_out_9, n1_bit_alu_10_out_9,
       n1_bit_alu_11_out_9, n1_bit_alu_12_out_9, n1_bit_alu_13_out_9, n1_bit_alu_14_out_9,
       n1_bit_alu_15_out_9;

  _1_bit_Alu u_1_bit_alu_1 (
    .A(A_input[0]), .Less(Set_less_than), .B(in_5[0]), .Result(out_6[0]), .out_9(n1_bit_alu_1_out_9),
    .Cin(Cin), .B_invert(Bin), .op_code(Alu_Op));  // open: Set
  _1_bit_Alu u_1_bit_alu_2 (
    .A(A_input[1]), .Less(1'b0), .B(in_5[1]), .Result(out_6[1]), .out_9(n1_bit_alu_2_out_9),
    .Cin(n1_bit_alu_1_out_9), .B_invert(Bin), .op_code(Alu_Op));  // open: Set
  _1_bit_Alu u_1_bit_alu_3 (
    .A(A_input[2]), .Less(1'b0), .B(in_5[2]), .Result(out_6[2]), .out_9(n1_bit_alu_3_out_9),
    .Cin(n1_bit_alu_2_out_9), .B_invert(Bin), .op_code(Alu_Op));  // open: Set
  _1_bit_Alu u_1_bit_alu_4 (
    .A(A_input[3]), .Less(1'b0), .B(in_5[3]), .Result(out_6[3]), .out_9(n1_bit_alu_4_out_9),
    .Cin(n1_bit_alu_3_out_9), .B_invert(Bin), .op_code(Alu_Op));  // open: Set
  _1_bit_Alu u_1_bit_alu_5 (
    .A(A_input[4]), .Less(1'b0), .B(in_5[4]), .Result(out_6[4]), .out_9(n1_bit_alu_5_out_9),
    .Cin(n1_bit_alu_4_out_9), .B_invert(Bin), .op_code(Alu_Op));  // open: Set
  _1_bit_Alu u_1_bit_alu_6 (
    .A(A_input[5]), .Less(1'b0), .B(in_5[5]), .Result(out_6[5]), .out_9(n1_bit_alu_6_out_9),
    .Cin(n1_bit_alu_5_out_9), .B_invert(Bin), .op_code(Alu_Op));  // open: Set
  _1_bit_Alu u_1_bit_alu_7 (
    .A(A_input[6]), .Less(1'b0), .B(in_5[6]), .Result(out_6[6]), .out_9(n1_bit_alu_7_out_9),
    .Cin(n1_bit_alu_6_out_9), .B_invert(Bin), .op_code(Alu_Op));  // open: Set
  _1_bit_Alu u_1_bit_alu_8 (
    .A(A_input[7]), .Less(1'b0), .B(in_5[7]), .Result(out_6[7]), .out_9(n1_bit_alu_8_out_9),
    .Cin(n1_bit_alu_7_out_9), .B_invert(Bin), .op_code(Alu_Op));  // open: Set
  _1_bit_Alu u_1_bit_alu_9 (
    .A(A_input[8]), .Less(1'b0), .B(in_5[8]), .Result(out_6[8]), .out_9(n1_bit_alu_9_out_9),
    .Cin(n1_bit_alu_8_out_9), .B_invert(Bin), .op_code(Alu_Op));  // open: Set
  _1_bit_Alu u_1_bit_alu_10 (
    .A(A_input[9]), .Less(1'b0), .B(in_5[9]), .Result(out_6[9]), .out_9(n1_bit_alu_10_out_9),
    .Cin(n1_bit_alu_9_out_9), .B_invert(Bin), .op_code(Alu_Op));  // open: Set
  _1_bit_Alu u_1_bit_alu_11 (
    .A(A_input[10]), .Less(1'b0), .B(in_5[10]), .Result(out_6[10]), .out_9(n1_bit_alu_11_out_9),
    .Cin(n1_bit_alu_10_out_9), .B_invert(Bin), .op_code(Alu_Op));  // open: Set
  _1_bit_Alu u_1_bit_alu_12 (
    .A(A_input[11]), .Less(1'b0), .B(in_5[11]), .Result(out_6[11]), .out_9(n1_bit_alu_12_out_9),
    .Cin(n1_bit_alu_11_out_9), .B_invert(Bin), .op_code(Alu_Op));  // open: Set
  _1_bit_Alu u_1_bit_alu_13 (
    .A(A_input[12]), .Less(1'b0), .B(in_5[12]), .Result(out_6[12]), .out_9(n1_bit_alu_13_out_9),
    .Cin(n1_bit_alu_12_out_9), .B_invert(Bin), .op_code(Alu_Op));  // open: Set
  _1_bit_Alu u_1_bit_alu_14 (
    .A(A_input[13]), .Less(1'b0), .B(in_5[13]), .Result(out_6[13]), .out_9(n1_bit_alu_14_out_9),
    .Cin(n1_bit_alu_13_out_9), .B_invert(Bin), .op_code(Alu_Op));  // open: Set
  _1_bit_Alu u_1_bit_alu_15 (
    .A(A_input[14]), .Less(1'b0), .B(in_5[14]), .Result(out_6[14]), .out_9(n1_bit_alu_15_out_9),
    .Cin(n1_bit_alu_14_out_9), .B_invert(Bin), .op_code(Alu_Op));  // open: Set
  _1_bit_Alu u_1_bit_alu_16 (
    .A(A_input[15]), .Less(1'b0), .B(in_5[15]), .Result(out_6[15]), .out_9(out_8), .Cin(n1_bit_alu_15_out_9),
    .B_invert(Bin), .op_code(Alu_Op), .Set(Set_less_than));
  nor nor_1 (Zero_detector, out_6[15], out_6[14], out_6[13], out_6[12], out_6[11], out_6[10], out_6[9], out_6[8], out_6[7], out_6[6], out_6[5], out_6[4], out_6[3], out_6[2], out_6[1], out_6[0]);

  // Notes on the sheet:
  //   B input
  //   set 0
  //   Result
  //   OVER FLOW
endmodule

module Full_Alu (
  input  Cin,
  input  B_invert,
  input  [15:0] in_3,
  input  [15:0] in_4,
  input  [2:0] AluOp,
  input  [1:0] SlSrSlt,
  output Zero_Detector,
  output out_8,
  output [15:0] out_9
);

  wire and_1_out, n16_bit_alu_1_set_less_than;
  wire [3:0] bit_extender_1_out;
  wire [15:0] multiplexer_2_out, n16_bit_alu_1_out_6, shifter_1_out, shifter_2_out;

  Bit_Extender #(.in_width(16), .out_width(4)) bit_extender_1 (.in(in_4), .out(bit_extender_1_out));
  _16_bit_Alu u_16_bit_alu_1 (
    .A_input(in_3), .in_5(in_4), .out_6(n16_bit_alu_1_out_6), .Zero_detector(Zero_Detector), .out_8(out_8),
    .Bin(B_invert), .Cin(Cin), .Alu_Op(AluOp), .Set_less_than(n16_bit_alu_1_set_less_than));
  Shifter #(.width(16)) shifter_1 (.in(in_3), .\dist (bit_extender_1_out), .out(shifter_1_out));
  Shifter #(.width(16), .shift("lr")) shifter_2 (.in(in_3), .\dist (bit_extender_1_out), .out(shifter_2_out));
  and and_1 (and_1_out, n16_bit_alu_1_set_less_than, 1'b1);
  Multiplexer #(.select(2), .width(16), .enable("false")) multiplexer_1 (
    .in0(n16_bit_alu_1_out_6), .in1(shifter_1_out), .in2(shifter_2_out), .in3(multiplexer_2_out),
    .out(out_9), .sel(SlSrSlt));
  Multiplexer #(.width(16), .enable("false")) multiplexer_2 (
    .in0({16{1'b0}}), .in1(16'h1), .out(multiplexer_2_out), .sel(and_1_out));

  // Notes on the sheet:
  //   input A
  //   input B
  //   Over Flow detector
  //   16 bit Alu
  //   output
  //   shift left
  //   shift right
  //   Set less than
endmodule

module main (
  input  Binv,
  input  Cin,
  input  [15:0] in_3,
  input  [15:0] in_4,
  input  [2:0] Alu_Op,
  input  [1:0] Shift,
  output Over_Flow,
  output [15:0] out_8,
  output Zero_Detector
);

  Full_Alu full_alu_1 (
    .in_3(in_3), .in_4(in_4), .Zero_Detector(Zero_Detector), .out_9(out_8), .B_invert(Binv), .Cin(Cin),
    .AluOp(Alu_Op), .out_8(Over_Flow), .SlSrSlt(Shift));

  // Notes on the sheet:
  //   A
  //   B
  //   Result
endmodule
