// Logisim project ControlSignal.circ as structural Verilog: 2 circuits, main circuit main
module main (
  input  [3:0] in_1,
  output out_2,
  output out_3,
  output out_4,
  output out_5,
  output out_6,
  output out_7,
  output [1:0] out_8,
  output [2:0] out_9,
  output [1:0] out_10,
  output out_11,
  output out_12,
  output out_13
);

  ControlSignal controlsignal_1 (
    .O3(in_1[3]), .O2(in_1[2]), .O1(in_1[1]), .O0(in_1[0]), .A2A1A0(out_9), .B0(out_3), .C0(out_4),
    .S1_S0(out_10), .R0(out_7), .AS1AS0(out_8), .RW(out_2), .MR(out_12), .MW(out_11), .MTR(out_13),
    .Br1(out_5), .Br2(out_6));

  // Notes on the sheet:
  //   Control Signal
endmodule

module ControlSignal (
  input  O3,
  input  O2,
  input  O1,
  input  O0,
  output [2:0] A2A1A0,
  output B0,
  output C0,
  output [1:0] S1_S0,
  output R0,
  output [1:0] AS1AS0,
  output RW,
  output MR,
  output MW,
  output MTR,
  output Br1,
  output Br2
);

  wire and_1_out, and_2_out, and_3_out, and_4_out, and_5_out, and_6_out, and_9_out, and_10_out, and_11_out,
       and_13_out, and_14_out, not_1_out, not_2_out, not_3_out, not_4_out, not_5_out, not_6_out, not_7_out,
       not_8_out, not_9_out, not_10_out, not_12_out, not_13_out, not_14_out, not_15_out, not_16_out,
       not_17_out, not_18_out;

  not not_1 (not_1_out, O3);
  not not_2 (not_2_out, O2);
  not not_3 (not_3_out, O3);
  not not_4 (not_4_out, O1);
  not not_5 (not_5_out, O3);
  and and_1 (and_1_out, not_5_out, O1, not_6_out);
  not not_6 (not_6_out, O0);
  not not_7 (not_7_out, O3);
  and and_2 (and_2_out, not_7_out, O2, not_8_out);
  not not_8 (not_8_out, O1);
  not not_9 (not_9_out, O3);
  and and_3 (and_3_out, not_9_out, O0);
  and and_4 (and_4_out, O1, O0);
  not not_10 (not_10_out, O3);
  and and_5 (and_5_out, not_10_out, O0);
  and and_6 (and_6_out, O1, O0);
  and and_7 (S1_S0[1], O2, O1);
  and and_8 (S1_S0[0], O2, O0);
  not not_11 (R0, O3);
  and and_9 (and_9_out, O2, not_12_out, O0);
  not not_12 (not_12_out, O1);
  and and_10 (and_10_out, O2, O1, not_13_out);
  not not_13 (not_13_out, O0);
  not not_14 (not_14_out, O3);
  not not_15 (not_15_out, O2);
  and and_11 (and_11_out, not_15_out, not_16_out);
  not not_16 (not_16_out, O1);
  not not_17 (not_17_out, O1);
  and and_12 (MR, O3, not_17_out, O0);
  not not_18 (not_18_out, O0);
  and and_13 (and_13_out, not_1_out, not_2_out, O1, O0);
  or or_1 (A2A1A0[1], and_13_out, and_14_out);
  and and_14 (and_14_out, not_3_out, O2, not_4_out);
  or or_2 (A2A1A0[0], and_1_out, and_2_out);
  or or_3 (B0, and_3_out, and_4_out, O2);
  or or_4 (C0, and_5_out, and_6_out, O2);
  or or_5 (AS1AS0[0], and_9_out, and_10_out);
  or or_6 (RW, not_14_out, and_11_out);
  and and_15 (MW, O3, O1, not_18_out);
  and and_16 (MTR, O3, O0);
  and and_17 (Br1, O3, O1, O0);
  and and_18 (Br2, O3, O2);

  assign A2A1A0[2] = 1'b0;
  assign AS1AS0[1] = O3;

  // Notes on the sheet:
  //   S0
  //   A2
  //   S1
  //   AS0
  //   A1
  //   A0
  //   AS1
endmodule
