// Logisim project DataPath.circ as structural Verilog: 1 circuit, main circuit main
module main (
  output Br2,
  output Br1,
  output [2:0] rs,
  output [2:0] rt,
  output RegWrite,
  output [15:0] out_6,
  output [15:0] out_7,
  output [2:0] rd,
  output Binv,
  output Cin,
  output [15:0] out_11,
  output zero,
  output [3:0] Op_12_15,
  output [15:0] out_14,
  output MemWrite,
  output out_16,
  output [2:0] AluOp,
  output [1:0] SlSrSlt,
  output MemToReg,
  output RegDst,
  output [1:0] AluSrc,
  output out_22
);

  wire beq_out, bne_out, CLK_out, not_1_out;
  wire [5:0] rom_1_data;
  wire [15:0] adder_1_out, adder_2_out, bit_extender_1_out, bit_extender_2_out, multiplexer_3_out,
       multiplexer_4_out, ram_1_data, register_1_q, registerfile_1_out_8, shifter_1_out;

  Register #(.width(16)) register_1 (.D(multiplexer_4_out), .Q(register_1_q), .clk(CLK_out));  // open: en, clr
  Clock CLK (.out(CLK_out));
  Adder #(.width(16)) adder_1 (.a(16'h1), .b(register_1_q), .out(adder_1_out));  // open: cin, cout
  ROM #(.addrWidth(16), .dataWidth(16)) rom_1 (
    .addr(register_1_q), .data({Op_12_15, rs, rt, rom_1_data}));  // open: sel
  ControlSignal controlsignal_1 (
    .O3(Op_12_15[3]), .O2(Op_12_15[2]), .O1(Op_12_15[1]), .O0(Op_12_15[0]), .A2A1A0(AluOp), .B0(Binv),
    .C0(Cin), .S1_S0(SlSrSlt), .R0(RegDst), .AS1AS0(AluSrc), .RW(RegWrite), .MR(out_16), .MW(MemWrite),
    .MTR(MemToReg), .Br1(Br1), .Br2(Br2));
  Multiplexer #(.width(3), .enable("false")) multiplexer_1 (.in0(rt), .in1(rom_1_data[5:3]), .out(rd), .sel(RegDst));
  RegisterFile registerfile_1 (
    .in_1(out_11), .out_7(out_6), .out_8(registerfile_1_out_8), .clk(CLK_out), .rt(rt), .rs(rs),
    .Data_Address(rd), .Reg_Write(RegWrite));
  assign bit_extender_1_out = {{13{1'b0}}, rom_1_data[2:0]};  // Bit_Extender bit_extender_1
  assign bit_extender_2_out = {{10{1'b0}}, rom_1_data};  // Bit_Extender bit_extender_2
  Multiplexer #(.select(2), .width(16), .enable("false")) multiplexer_2 (
    .in0(registerfile_1_out_8), .in1(bit_extender_1_out), .in2(bit_extender_2_out), .out(out_7), .sel(AluSrc));  // open: in3
  Shifter #(.width(16)) shifter_1 (.in(bit_extender_2_out), .\dist (4'b0001), .out(shifter_1_out));
  Adder #(.width(16)) adder_2 (.a(adder_1_out), .b(shifter_1_out), .out(adder_2_out));  // open: cin, cout
  Full_Alu full_alu_1 (
    .in_3(out_6), .in_4(out_7), .Zero_Detector(zero), .out_9(out_14), .B_invert(Binv), .Cin(Cin),
    .AluOp(AluOp), .SlSrSlt(SlSrSlt));  // open: out_8
  Multiplexer #(.width(16), .enable("false")) multiplexer_3 (
    .in0(adder_1_out), .in1(adder_2_out), .out(multiplexer_3_out), .sel(beq_out));
  and beq (beq_out, Br1, zero);
  not not_1 (not_1_out, zero);
  and bne (bne_out, Br2, not_1_out);
  Multiplexer #(.width(16), .enable("false")) multiplexer_4 (
    .in0(multiplexer_3_out), .in1(adder_2_out), .out(multiplexer_4_out), .sel(bne_out));
  RAM #(.addrWidth(16), .dataWidth(16), .bus("separate")) ram_1 (
    .addr(out_14), .data(ram_1_data), .str(MemWrite), .clk(CLK_out), .ld(out_16));  // open: din, sel, clr
  Multiplexer #(.width(16), .enable("false")) multiplexer_5 (
    .in0(out_14), .in1(ram_1_data), .out(out_11), .sel(MemToReg));

  // Notes on the sheet:
  //   contents of rom_1 (hex, n*v repeats v):
  //   969e 94de 955e 9b9e 1b30 8362 a69e a654 20d0 4518 512b 612b de8 b184 ca08 7dd8
  //   [9-11]
  //   Rs
  //   Rd[3-5]
  //   Rt [6-8]
  //   data 1
  //   MemToReg
  //   MemRead
  //   MemWrite
  //   SlSrSlt
  //   AluOp
  //   AluSrc
  //   data 2
  //   Shmt[0-2]
  //   [0-5]
  //   Itype
  //   Shift left 1
  //   MemRead
endmodule
