// Logisim project Reg-final.circ as structural Verilog: 2 circuits, main circuit main
module main (
);

  RegisterFile registerfile_1 ();  // open: in_1, out_7, out_8, clk, rt, rs, Data_Address, Reg_Write
endmodule

module RegisterFile (
  input  [15:0] in_1,
  input  Reg_Write,
  input  [2:0] Data_Address,
  input  [2:0] rt,
  input  [2:0] rs,
  input  clk,
  output [15:0] out_7,
  output [15:0] out_8
);

  wire and_1_out, and_2_out, and_3_out, and_4_out, and_5_out, and_6_out, and_7_out, and_8_out,
       decoder_1_out0, decoder_1_out1, decoder_1_out2, decoder_1_out3, decoder_1_out4, decoder_1_out5,
       decoder_1_out6, decoder_1_out7;
  wire [15:0] register_1_q, register_2_q, register_3_q, register_4_q, register_5_q, register_6_q,
       register_7_q, register_8_q;

  Decoder #(.select(3)) decoder_1 (
    .out0(decoder_1_out0), .out1(decoder_1_out1), .out2(decoder_1_out2), .out3(decoder_1_out3),
    .out4(decoder_1_out4), .out5(decoder_1_out5), .out6(decoder_1_out6), .out7(decoder_1_out7),
    .sel(Data_Address));  // open: en
  and and_1 (and_1_out, Reg_Write, decoder_1_out0);
  and and_2 (and_2_out, Reg_Write, decoder_1_out1);
  and and_3 (and_3_out, Reg_Write, decoder_1_out2);
  and and_4 (and_4_out, Reg_Write, decoder_1_out3);
  and and_5 (and_5_out, Reg_Write, decoder_1_out4);
  and and_6 (and_6_out, Reg_Write, decoder_1_out5);
  and and_7 (and_7_out, Reg_Write, decoder_1_out6);
  and and_8 (and_8_out, Reg_Write, decoder_1_out7);
  Register #(.width(16)) register_1 (.D({16{1'b0}}), .en(and_1_out), .Q(register_1_q), .clk(clk));  // open: clr
  Register #(.width(16)) register_2 (.D(in_1), .en(and_2_out), .Q(register_2_q), .clk(clk));  // open: clr
  Register #(.width(16)) register_3 (.D(in_1), .en(and_3_out), .Q(register_3_q), .clk(clk));  // open: clr
  Register #(.width(16)) register_4 (.D(in_1), .en(and_4_out), .Q(register_4_q), .clk(clk));  // open: clr
  Register #(.width(16)) register_5 (.D(in_1), .en(and_5_out), .Q(register_5_q), .clk(clk));  // open: clr
  Register #(.width(16)) register_6 (.D(in_1), .en(and_6_out), .Q(register_6_q), .clk(clk));  // open: clr
  Register #(.width(16)) register_7 (.D(in_1), .en(and_7_out), .Q(register_7_q), .clk(clk));  // open: clr
  Register #(.width(16)) register_8 (.D(in_1), .en(and_8_out), .Q(register_8_q), .clk(clk));  // open: clr
  Multiplexer #(.select(3), .width(16), .enable("false")) multiplexer_1 (
    .in0(register_1_q), .in1(register_2_q), .in2(register_3_q), .in3(register_4_q), .in4(register_5_q),
    .in5(register_6_q), .in6(register_7_q), .in7(register_8_q), .out(out_8), .sel(rt));
  Multiplexer #(.select(3), .width(16), .enable("false")) multiplexer_2 (
    .in0(register_1_q), .in1(register_2_q), .in2(register_3_q), .in3(register_4_q), .in4(register_5_q),
    .in5(register_6_q), .in6(register_7_q), .in7(register_8_q), .out(out_7), .sel(rs));

  // Notes on the sheet:
  //   Data In
  //   zero register
  //   data 01
  //   data 02
endmodule
