// Logisim project TicTacToe.circ as structural Verilog: 6 circuits, main circuit main
module main (
  input  Power
);

  wire button_1_out, button_2_out, button_3_out, button_4_out, button_5_out, button_6_out, button_7_out,
       button_8_out, button_9_out, button_10_out, switch_1__1a, switch_1__1b, switch_1__2a, switch_1__2b,
       switch_1__3a, switch_1__3b, switch_1__4a, switch_1__4b, switch_1__6a, switch_1__6b, switch_1__7a,
       switch_1__7b, switch_1__8a, switch_1__8b, switch_1__9a, switch_1__9b, switch_1_draw, switch_1_out_12,
       switch_1_out_21, switch_1_out_22, switch_1_out_32;

  Button button_1 (.out(button_1_out));
  Button button_2 (.out(button_2_out));
  Button button_3 (.out(button_3_out));
  Button button_4 (.out(button_4_out));
  Button button_5 (.out(button_5_out));
  Button button_6 (.out(button_6_out));
  Button button_7 (.out(button_7_out));
  Button button_8 (.out(button_8_out));
  Button button_9 (.out(button_9_out));
  Button button_10 (.out(button_10_out));
  Switch switch_1 (
    .power(Power), .in_2(button_4_out), .sw1(button_1_out), .sw2(button_5_out), .sw3(button_8_out),
    .sw4(button_2_out), .sw5(button_6_out), .sw6(button_9_out), .sw7(button_3_out), .sw8(button_7_out),
    .sw9(button_10_out), .out_12(switch_1_out_12), .Draw(switch_1_draw), .out_32(switch_1_out_32),
    ._4a(switch_1__4a), ._7a(switch_1__7a), ._4b(switch_1__4b), ._7b(switch_1__7b), .out_21(switch_1_out_21),
    ._8a(switch_1__8a), .out_22(switch_1_out_22), ._8b(switch_1__8b), ._6a(switch_1__6a), ._9a(switch_1__9a),
    ._6b(switch_1__6b), ._9b(switch_1__9b), ._1a(switch_1__1a), ._1b(switch_1__1b), ._2a(switch_1__2a),
    ._2b(switch_1__2b), ._3a(switch_1__3a), ._3b(switch_1__3b));
  LED led_1 (.in(switch_1_out_12));
  LED led_2 (.in(switch_1_out_32));
  LED led_3 (.in(switch_1__1b));
  LED led_4 (.in(switch_1__1a));
  LED led_5 (.in(switch_1__4a));
  LED led_6 (.in(switch_1__4b));
  LED led_7 (.in(switch_1__7a));
  LED led_8 (.in(switch_1__7b));
  LED led_9 (.in(switch_1__2a));
  LED led_10 (.in(switch_1_out_21));
  LED led_11 (.in(switch_1__8a));
  LED led_12 (.in(switch_1_draw));
  LED led_13 (.in(switch_1__3a));
  LED led_14 (.in(switch_1__2b));
  LED led_15 (.in(switch_1__6a));
  LED led_16 (.in(switch_1_out_22));
  LED led_17 (.in(switch_1__9a));
  LED led_18 (.in(switch_1__8b));
  LED led_19 (.in(switch_1__3b));
  LED led_20 (.in(switch_1__6b));
  LED led_21 (.in(switch_1__9b));

  // Notes on the sheet:
  //   Reset
  //   TIC TAC TOE
  //   WINNER
  //   DRAW
endmodule

module saveData (
  input  A_input,
  input  Start,
  input  Power,
  input  Re_Set,
  input  B_input,
  output Player_1_s_input,
  output Player_2_s_input
);

  wire d_ff_1_q, undriven, undriven_2;

  D_Flip_Flop d_ff_1 (
    .clk(Start), .D(Power), .Q(d_ff_1_q), .preset(undriven), .en(undriven), .reset(Re_Set));  // open: Qn
  D_Flip_Flop d_ff_2 (
    .clk(d_ff_1_q), .D(A_input), .Q(Player_1_s_input), .preset(undriven_2), .en(undriven_2), .reset(Re_Set));  // open: Qn
  D_Flip_Flop d_ff_3 (.clk(d_ff_1_q), .D(B_input), .Q(Player_2_s_input), .reset(Re_Set));  // open: Qn, preset, en

  // Notes on the sheet:
  //   (Connected to individual switch)
  //   (comes from tracking circuit )
  //   (comes from tracking circuit )
  //   Circut to Save Player's Input
endmodule

module Profile (
  input  sw1,
  input  in_2,
  input  sw2,
  input  in_4,
  input  sw3,
  input  in_6,
  input  sw4,
  input  in_8,
  input  sw5,
  input  in_10,
  input  sw6,
  input  in_12,
  input  sw7,
  input  in_14,
  input  sw8,
  input  in_16,
  input  sw9,
  input  in_18,
  output Player_1_s_trun,
  output out_20
);

  wire xor_1_out, xor_2_out, xor_3_out, xor_4_out, xor_5_out, xor_6_out, xor_7_out, xor_8_out, xor_9_out,
       xor_10_out, xor_11_out, xor_12_out, xor_13_out, xor_14_out, xor_15_out, xor_16_out;

  xor xor_1 (xor_1_out, sw1, in_2);
  xor xor_2 (xor_2_out, sw2, in_4);
  xor xor_3 (xor_3_out, sw3, in_6);
  xor xor_4 (xor_4_out, sw4, in_8);
  xor xor_5 (xor_5_out, sw5, in_10);
  xor xor_6 (xor_6_out, sw6, in_12);
  xor xor_7 (xor_7_out, sw7, in_14);
  xor xor_8 (xor_8_out, sw8, in_16);
  xor xor_9 (xor_9_out, sw9, in_18);
  xor xor_10 (xor_10_out, xor_1_out, xor_2_out);
  xor xor_11 (xor_11_out, xor_3_out, xor_4_out);
  xor xor_12 (xor_12_out, xor_5_out, xor_6_out);
  xor xor_13 (xor_13_out, xor_7_out, xor_8_out);
  xor xor_14 (xor_14_out, xor_10_out, xor_11_out);
  xor xor_15 (xor_15_out, xor_12_out, xor_13_out);
  xor xor_16 (xor_16_out, xor_14_out, xor_15_out);
  xor xor_17 (Player_1_s_trun, xor_16_out, xor_9_out);
  not not_1 (out_20, Player_1_s_trun);

  // Notes on the sheet:
  //   Circut to track Player's Turn
  //   Player 2's turn
endmodule

module winningCombination (
  input  in_1,
  input  in_2,
  input  in_3,
  input  in_4,
  input  in_5,
  input  in_6,
  input  in_7,
  input  in_8,
  input  in_9,
  output out_10
);

  wire and_1_out, and_2_out, and_3_out, and_4_out, and_5_out, and_6_out, and_7_out, and_8_out, or_1_out,
       or_2_out, or_3_out;

  and and_1 (and_1_out, in_1, in_2, in_3);
  and and_2 (and_2_out, in_4, in_5, in_6);
  and and_3 (and_3_out, in_7, in_8, in_9);
  and and_4 (and_4_out, in_1, in_4, in_7);
  and and_5 (and_5_out, in_2, in_5, in_8);
  and and_6 (and_6_out, in_3, in_6, in_9);
  or or_1 (or_1_out, and_1_out, and_2_out, and_3_out);
  and and_7 (and_7_out, in_1, in_5, in_9);
  and and_8 (and_8_out, in_5, in_3, in_7);
  or or_2 (or_2_out, and_4_out, and_5_out, and_6_out);
  or or_3 (or_3_out, and_7_out, and_8_out);
  or or_4 (out_10, or_1_out, or_3_out, or_2_out);

  // Notes on the sheet:
  //   1
  //   2
  //   3
  //   4
  //   5
  //   6
  //   7
  //   8
  //   9
  //   1
  //   2
  //   3
  //   4
  //   5
  //   6
  //   7
  //   8
  //   9
  //   1
  //   4
  //   7
  //   2
  //   5
  //   8
  //   3
  //   6
  //   9
  //   Circuit of  Winning Combinations
  //   1
  //   5
  //   9
  //   5
  //   3
  //   7
endmodule

module Draw_Combination (
  input  _1,
  input  _2,
  input  _3,
  input  _4,
  input  _5,
  input  _6,
  input  _7,
  input  _8,
  input  _9,
  output out_10
);

  wire and_1_out, and_2_out, and_3_out;

  and and_1 (and_1_out, _1, _2, _3);
  and and_2 (and_2_out, _4, _5, _6);
  and and_3 (and_3_out, _7, _8, _9);
  and and_4 (out_10, and_1_out, and_2_out, and_3_out);

  // Notes on the sheet:
  //   Circuit for checking DRAW combinations
endmodule

module Switch (
  input  power,
  input  in_2,
  input  sw1,
  input  sw2,
  input  sw3,
  input  sw4,
  input  sw5,
  input  sw6,
  input  sw7,
  input  sw8,
  input  sw9,
  output out_12,
  output _1a,
  output _1b,
  output _2a,
  output _2b,
  output _3a,
  output _3b,
  output _4a,
  output _4b,
  output out_21,
  output out_22,
  output _6a,
  output _6b,
  output Draw,
  output _7a,
  output _7b,
  output _8a,
  output _8b,
  output _9a,
  output _9b,
  output out_32
);

  wire and_1_out, and_2_out, and_3_out, and_4_out, and_5_out, and_6_out, and_7_out, and_8_out, and_9_out,
       and_10_out, and_11_out, and_12_out, and_13_out, and_14_out, not_1_out, or_1_out, or_2_out, or_3_out,
       or_4_out, or_5_out, or_6_out, or_7_out, or_8_out, or_9_out, or_10_out, profile_1_out_20,
       profile_1_player_1_s_trun;

  and and_1 (and_1_out, sw1, not_1_out);
  and and_2 (and_2_out, sw8, not_1_out);
  and and_3 (and_3_out, sw9, not_1_out);
  and and_4 (and_4_out, sw2, not_1_out);
  and and_5 (and_5_out, sw3, not_1_out);
  and and_6 (and_6_out, sw4, not_1_out);
  and and_7 (and_7_out, sw5, not_1_out);
  and and_8 (and_8_out, sw6, not_1_out);
  and and_9 (and_9_out, sw7, not_1_out);
  saveData savedata_1 (
    .A_input(profile_1_player_1_s_trun), .B_input(profile_1_out_20), .Start(and_1_out), .Re_Set(in_2),
    .Player_1_s_input(_1b), .Player_2_s_input(_1a), .Power(power));
  saveData savedata_2 (
    .A_input(profile_1_player_1_s_trun), .B_input(profile_1_out_20), .Start(and_4_out), .Re_Set(in_2),
    .Player_1_s_input(_2b), .Player_2_s_input(_2a), .Power(power));
  saveData savedata_3 (
    .A_input(profile_1_player_1_s_trun), .B_input(profile_1_out_20), .Start(and_5_out), .Re_Set(in_2),
    .Player_1_s_input(_3b), .Player_2_s_input(_3a), .Power(power));
  saveData savedata_4 (
    .A_input(profile_1_player_1_s_trun), .B_input(profile_1_out_20), .Start(and_6_out), .Re_Set(in_2),
    .Player_1_s_input(_4b), .Player_2_s_input(_4a), .Power(power));
  saveData savedata_5 (
    .A_input(profile_1_player_1_s_trun), .B_input(profile_1_out_20), .Start(and_7_out), .Re_Set(in_2),
    .Player_1_s_input(out_22), .Player_2_s_input(out_21), .Power(power));
  saveData savedata_6 (
    .A_input(profile_1_player_1_s_trun), .B_input(profile_1_out_20), .Start(and_8_out), .Re_Set(in_2),
    .Player_1_s_input(_6b), .Player_2_s_input(_6a), .Power(power));
  saveData savedata_7 (
    .A_input(profile_1_player_1_s_trun), .B_input(profile_1_out_20), .Start(and_9_out), .Re_Set(in_2),
    .Player_1_s_input(_7b), .Player_2_s_input(_7a), .Power(power));
  saveData savedata_8 (
    .A_input(profile_1_player_1_s_trun), .B_input(profile_1_out_20), .Start(and_2_out), .Re_Set(in_2),
    .Player_1_s_input(_8b), .Player_2_s_input(_8a), .Power(power));
  saveData savedata_9 (
    .A_input(profile_1_player_1_s_trun), .B_input(profile_1_out_20), .Start(and_3_out), .Re_Set(in_2),
    .Player_1_s_input(_9b), .Player_2_s_input(_9a), .Power(power));
  Profile profile_1 (
    .sw1(_1b), .in_2(_1a), .sw2(_2b), .in_4(_2a), .sw3(_3b), .in_6(_3a), .sw4(_4b), .in_8(_4a),
    .Player_1_s_trun(profile_1_player_1_s_trun), .out_20(profile_1_out_20), .sw5(out_22), .in_10(out_21),
    .sw6(_6b), .in_12(_6a), .sw7(_7b), .in_14(_7a), .sw8(_8b), .in_16(_8a), .sw9(_9b), .in_18(_9a));
  winningCombination winningcombination_1 (
    .in_1(_1b), .in_2(_2b), .in_3(_3b), .in_4(_4b), .in_5(out_22), .in_6(_6b), .in_7(_7b), .in_8(_8b),
    .in_9(_9b), .out_10(out_32));
  winningCombination winningcombination_2 (
    .in_1(_1a), .in_2(_2a), .in_3(_3a), .in_4(_4a), .in_5(out_21), .in_6(_6a), .in_7(_7a), .in_8(_8a),
    .in_9(_9a), .out_10(out_12));
  or or_1 (or_1_out, _8a, _8b);
  or or_2 (or_2_out, _7a, _7b);
  or or_3 (or_3_out, _1a, _1b);
  or or_4 (or_4_out, _2b, _2a);
  or or_5 (or_5_out, _3b, _3a);
  or or_6 (or_6_out, _4b, _4a);
  or or_7 (or_7_out, _6b, _6a);
  or or_8 (or_8_out, out_22, out_21);
  or or_9 (or_9_out, out_12, out_32);
  not not_1 (not_1_out, or_9_out);
  or or_10 (or_10_out, _9b, _9a);
  and and_10 (and_10_out, or_3_out, or_4_out, or_5_out);
  and and_11 (and_11_out, or_1_out, or_10_out, or_2_out);
  and and_12 (and_12_out, or_6_out, or_7_out, or_8_out);
  and and_13 (and_13_out, and_10_out, and_12_out);
  and and_14 (and_14_out, not_1_out, and_11_out);
  and and_15 (Draw, and_13_out, and_14_out);

  // Notes on the sheet:
  //   Reset
  //   input1
  //   input2
  //   input3
  //   input9
  //   input8
  //   input7
  //   input4
  //   input6
  //   input5
endmodule
